// Logisim project newCpu.circ as structural Verilog: 2 circuits, main circuit main
module main (
);

  wire button_1_out, button_2_out, button_3_out, button_4_out, clock_1_out, dipswitch_1_sw1, dipswitch_1_sw2,
       dipswitch_1_sw3, dipswitch_1_sw4, inputflop_1_out_10, inputflop_1_out_11, inputflop_1_out_12,
       inputflop_1_out_13, inputflop_1_out_14, inputflop_1_out_15, inputflop_1_out_16, inputflop_1_out_17,
       inputflop_1_out_18, inputflop_1_out_19, inputflop_1_out_20, inputflop_1_out_21, inputflop_1_out_22,
       inputflop_1_out_23, inputflop_1_out_24, inputflop_1_out_25;

  DipSwitch #(.number(4)) dipswitch_1 (
    .sw1(dipswitch_1_sw1), .sw2(dipswitch_1_sw2), .sw3(dipswitch_1_sw3), .sw4(dipswitch_1_sw4));
  TTY tty_1 ();  // open: data, clk, we, clr
  Button button_1 (.out(button_1_out));
  Button button_2 (.out(button_2_out));
  Button button_3 (.out(button_3_out));
  Button button_4 (.out(button_4_out));
  Clock clock_1 (.out(clock_1_out));
  inputflop inputflop_1 (
    .d1(dipswitch_1_sw1), .d2(dipswitch_1_sw2), .d3(dipswitch_1_sw3), .d4(dipswitch_1_sw4),
    .b1(button_1_out), .b2(button_2_out), .b3(button_3_out), .b4(button_4_out), .clk(clock_1_out),
    .out_10(inputflop_1_out_10), .out_11(inputflop_1_out_11), .out_12(inputflop_1_out_12),
    .out_13(inputflop_1_out_13), .out_14(inputflop_1_out_14), .out_15(inputflop_1_out_15),
    .out_16(inputflop_1_out_16), .out_17(inputflop_1_out_17), .out_18(inputflop_1_out_18),
    .out_19(inputflop_1_out_19), .out_20(inputflop_1_out_20), .out_21(inputflop_1_out_21),
    .out_22(inputflop_1_out_22), .out_23(inputflop_1_out_23), .out_24(inputflop_1_out_24),
    .out_25(inputflop_1_out_25));
  LED led_1 (.in(inputflop_1_out_10));
  LED led_2 (.in(inputflop_1_out_11));
  LED led_3 (.in(inputflop_1_out_12));
  LED led_4 (.in(inputflop_1_out_13));
  LED led_5 (.in(inputflop_1_out_14));
  LED led_6 (.in(inputflop_1_out_15));
  LED led_7 (.in(inputflop_1_out_16));
  LED led_8 (.in(inputflop_1_out_17));
  LED led_9 (.in(inputflop_1_out_18));
  LED led_10 (.in(inputflop_1_out_19));
  LED led_11 (.in(inputflop_1_out_20));
  LED led_12 (.in(inputflop_1_out_21));
  LED led_13 (.in(inputflop_1_out_22));
  LED led_14 (.in(inputflop_1_out_23));
  LED led_15 (.in(inputflop_1_out_24));
  LED led_16 (.in(inputflop_1_out_25));
endmodule

module inputflop (
  input  d1,
  input  d2,
  input  d3,
  input  d4,
  input  b1,
  input  b2,
  input  b3,
  input  b4,
  input  clk,
  output out_10,
  output out_11,
  output out_12,
  output out_13,
  output out_14,
  output out_15,
  output out_16,
  output out_17,
  output out_18,
  output out_19,
  output out_20,
  output out_21,
  output out_22,
  output out_23,
  output out_24,
  output out_25
);

  wire and_1_out, and_2_out, and_3_out, and_4_out, and_5_out, and_6_out, and_7_out, and_8_out, and_9_out,
       and_10_out, and_11_out, and_12_out, and_13_out, and_14_out, and_15_out, and_16_out, or_1_out,
       or_2_out, or_3_out, or_4_out, s_r_ff_1_q, s_r_ff_2_q, s_r_ff_3_q, s_r_ff_4_q;

  or or_1 (or_1_out, b2, b3, b4);
  or or_2 (or_2_out, b1, b3, b4);
  or or_3 (or_3_out, b1, b2, b4);
  or or_4 (or_4_out, b1, b2, b3);
  S_R_Flip_Flop s_r_ff_1 (.S(b1), .R(or_1_out), .clk(clk), .Q(s_r_ff_1_q));  // open: reset, Qn, preset
  S_R_Flip_Flop s_r_ff_2 (.S(b2), .R(or_2_out), .clk(clk), .Q(s_r_ff_2_q));  // open: reset, Qn, preset
  S_R_Flip_Flop s_r_ff_3 (.S(b3), .R(or_3_out), .clk(clk), .Q(s_r_ff_3_q));  // open: reset, Qn, preset
  S_R_Flip_Flop s_r_ff_4 (.S(b4), .R(or_4_out), .clk(clk), .Q(s_r_ff_4_q));  // open: reset, Qn, preset
  and and_1 (and_1_out, d1, s_r_ff_1_q);
  and and_2 (and_2_out, d3, s_r_ff_1_q);
  and and_3 (and_3_out, d1, s_r_ff_2_q);
  and and_4 (and_4_out, d2, s_r_ff_2_q);
  and and_5 (and_5_out, d3, s_r_ff_2_q);
  and and_6 (and_6_out, d4, s_r_ff_2_q);
  and and_7 (and_7_out, d1, s_r_ff_3_q);
  and and_8 (and_8_out, d2, s_r_ff_3_q);
  and and_9 (and_9_out, d3, s_r_ff_3_q);
  and and_10 (and_10_out, d4, s_r_ff_3_q);
  and and_11 (and_11_out, d1, s_r_ff_4_q);
  and and_12 (and_12_out, d2, s_r_ff_4_q);
  and and_13 (and_13_out, d3, s_r_ff_4_q);
  and and_14 (and_14_out, d4, s_r_ff_4_q);
  and and_15 (and_15_out, s_r_ff_1_q, d2);
  and and_16 (and_16_out, d4, s_r_ff_1_q);
  Register #(.width(1)) register_1 (.D(and_1_out), .en(s_r_ff_1_q), .Q(out_10), .clk(clk));  // open: clr
  Register #(.width(1)) register_2 (.D(and_15_out), .en(s_r_ff_1_q), .Q(out_11), .clk(clk));  // open: clr
  Register #(.width(1)) register_3 (.D(and_2_out), .en(s_r_ff_1_q), .Q(out_12), .clk(clk));  // open: clr
  Register #(.width(1)) register_4 (.D(and_16_out), .en(s_r_ff_1_q), .Q(out_13), .clk(clk));  // open: clr
  Register #(.width(1)) register_5 (.D(and_3_out), .en(s_r_ff_2_q), .Q(out_14), .clk(clk));  // open: clr
  Register #(.width(1)) register_6 (.D(and_4_out), .en(s_r_ff_2_q), .Q(out_15), .clk(clk));  // open: clr
  Register #(.width(1)) register_7 (.D(and_5_out), .en(s_r_ff_2_q), .Q(out_16), .clk(clk));  // open: clr
  Register #(.width(1)) register_8 (.D(and_6_out), .en(s_r_ff_2_q), .Q(out_17), .clk(clk));  // open: clr
  Register #(.width(1)) register_9 (.D(and_7_out), .Q(out_18), .clk(clk));  // open: en, clr
  Register #(.width(1)) register_10 (.D(and_8_out), .Q(out_19), .clk(clk));  // open: en, clr
  Register #(.width(1)) register_11 (.D(and_9_out), .Q(out_20), .clk(clk));  // open: en, clr
  Register #(.width(1)) register_12 (.D(and_10_out), .Q(out_21), .clk(clk));  // open: en, clr
  Register #(.width(1)) register_13 (.D(and_11_out), .en(s_r_ff_4_q), .Q(out_22), .clk(clk));  // open: clr
  Register #(.width(1)) register_14 (.D(and_12_out), .en(s_r_ff_4_q), .Q(out_23), .clk(clk));  // open: clr
  Register #(.width(1)) register_15 (.D(and_13_out), .Q(out_24), .clk(clk));  // open: en, clr
  Register #(.width(1)) register_16 (.D(and_14_out), .en(s_r_ff_4_q), .Q(out_25), .clk(clk));  // open: clr
endmodule
